// Digital circuit ALU COMPLETO.dig as structural Verilog
module ALU_COMPLETO (
  input  A,
  input  B,
  input  A_2,
  input  B_2,
  input  Cin,
  input  A0,
  input  A1,
  input  A2,
  input  A3,
  input  B0,
  input  B1,
  input  B2,
  input  B3,
  input  A_3,
  input  B_3,
  input  Cin_2,
  input  A_4,
  input  B_4,
  input  Cin_3,
  input  A_5,
  input  B_5,
  input  Cin_4,
  input  A_6,
  input  B_6,
  input  Cin_5,
  input  A0_2,
  input  A1_2,
  input  A2_2,
  input  A3_2,
  input  A4,
  input  A5,
  input  A6,
  input  A7,
  input  B0_2,
  input  B1_2,
  input  B2_2,
  input  B3_2,
  input  B4,
  input  B5,
  input  B6,
  input  B7,
  input  Cin_6,
  input  A8,
  input  A9,
  input  A10,
  input  A11,
  input  A12,
  input  A13,
  input  A14,
  input  A15,
  input  B8,
  input  B9,
  input  B10,
  input  B11,
  input  B12,
  input  B13,
  input  B14,
  input  B15,
  input  Cin_7,
  input  A0_3,
  input  A1_3,
  input  A2_3,
  input  A3_3,
  input  A4_2,
  input  A5_2,
  input  A6_2,
  input  A7_2,
  input  B0_3,
  input  B1_3,
  input  B2_3,
  input  B3_3,
  input  B4_2,
  input  B5_2,
  input  B6_2,
  input  B7_2,
  input  Sub,
  input  A0_4,
  input  A1_4,
  input  A2_4,
  input  A3_4,
  input  A4_3,
  input  A5_3,
  input  A6_3,
  input  A7_3,
  input  B0_4,
  input  B1_4,
  input  B2_4,
  input  B3_4,
  input  B4_3,
  input  B5_3,
  input  B6_3,
  input  B7_3,
  input  A0_5,
  input  A1_5,
  input  A2_5,
  input  A3_5,
  input  B0_5,
  input  B1_5,
  input  B2_5,
  input  B3_5,
  input  A0_6,
  input  A1_6,
  input  A2_6,
  input  A3_6,
  input  B0_6,
  input  B1_6,
  input  B2_6,
  input  B3_6,
  input  A1_7,
  input  A2_7,
  input  A3_7,
  input  A4_4,
  input  A5_4,
  input  A6_4,
  input  A7_4,
  input  A0_7,
  input  A17,
  input  A18,
  input  A19,
  input  A20,
  input  A21,
  input  A22,
  input  A23,
  input  A16,
  input  A1_8,
  input  A2_8,
  input  A3_8,
  input  A4_5,
  input  A5_5,
  input  A6_5,
  input  A7_5,
  input  A0_8,
  input  A25,
  input  A26,
  input  A27,
  input  A28,
  input  A29,
  input  A30,
  input  A31,
  input  A24,
  input  A0_9,
  input  A1_9,
  input  A2_9,
  input  A3_9,
  input  A4_6,
  input  A5_6,
  input  A6_6,
  input  A7_6,
  input  B0_7,
  input  B1_7,
  input  B2_7,
  input  B3_7,
  input  B4_4,
  input  B5_4,
  input  B6_4,
  input  B7_4,
  input  A32,
  input  A33,
  input  A34,
  input  A35,
  input  A36,
  input  A37,
  input  A38,
  input  A39,
  input  B16,
  input  B17,
  input  B18,
  input  B19,
  input  B20,
  input  B21,
  input  B22,
  input  B23,
  input  A0_10,
  input  A1_10,
  input  A2_10,
  input  A3_10,
  input  A4_7,
  input  A5_7,
  input  A6_7,
  input  A7_7,
  input  B0_8,
  input  B1_8,
  input  B2_8,
  input  B3_8,
  input  B4_5,
  input  B5_5,
  input  B6_5,
  input  B7_5,
  input  A40,
  input  A41,
  input  A42,
  input  A43,
  input  A44,
  input  A45,
  input  A46,
  input  A47,
  input  B24,
  input  B25,
  input  B26,
  input  B27,
  input  B28,
  input  B29,
  input  B30,
  input  B31,
  input  A0_11,
  input  A1_11,
  input  A2_11,
  input  A3_11,
  input  A4_8,
  input  A5_8,
  input  A6_8,
  input  A7_8,
  input  B0_9,
  input  B1_9,
  input  B2_9,
  input  B3_9,
  input  B4_6,
  input  B5_6,
  input  B6_6,
  input  B7_6,
  input  A48,
  input  A49,
  input  A50,
  input  A51,
  input  A52,
  input  A53,
  input  A54,
  input  A55,
  input  B32,
  input  B33,
  input  B34,
  input  B35,
  input  B36,
  input  B37,
  input  B38,
  input  B39,
  input  SEL_0,
  input  SEL_1,
  input  SEL_2,
  input  A0_12,
  input  A1_12,
  input  A2_12,
  input  A3_12,
  input  A4_9,
  input  A5_9,
  input  A6_9,
  input  A7_9,
  input  B0_10,
  input  B1_10,
  input  B2_10,
  input  B3_10,
  input  B4_7,
  input  B5_7,
  input  B6_7,
  input  B7_7,
  output Soma,
  output Carry,
  output Soma_2,
  output Carry_Out,
  output S0,
  output S1,
  output S2,
  output S3,
  output OVERFLOW,
  output S0_2,
  output S1_2,
  output S2_2,
  output S3_2,
  output S4,
  output S5,
  output S6,
  output S7,
  output Cout,
  output out_78,
  output out_95,
  output Cout_2,
  output MULT_BIT0,
  output MULT_BIT1,
  output MULT_BIT2,
  output MULT_BIT3,
  output MULT_BIT4,
  output MULT_BIT5,
  output MULT_BIT6,
  output MULT_BIT7,
  output [7:0] Multiplicador,
  output SR_BIT0,
  output SR_BIT1,
  output SR_BIT2,
  output SR_BIT3,
  output SR_BIT4,
  output SR_BIT5,
  output SR_BIT6,
  output SR_BIT7,
  output [7:0] SR,
  output SL_BIT0,
  output SL_BIT1,
  output SL_BIT2,
  output SL_BIT3,
  output SL_BIT4,
  output SL_BIT5,
  output SL_BIT6,
  output SL_BIT7,
  output [7:0] SL,
  output AND_BIT0,
  output AND_BIT1,
  output AND_BIT2,
  output AND_BIT3,
  output AND_BIT4,
  output AND_BIT5,
  output AND_BIT6,
  output AND_BIT7,
  output [7:0] AND,
  output OR_BIT0,
  output OR_BIT1,
  output OR_BIT2,
  output OR_BIT3,
  output OR_BIT4,
  output OR_BIT5,
  output OR_BIT6,
  output OR_BIT7,
  output [7:0] OR,
  output XOR_BIT0,
  output XOR_BIT1,
  output XOR_BIT2,
  output XOR_BIT3,
  output XOR_BIT4,
  output XOR_BIT5,
  output XOR_BIT6,
  output XOR_BIT7,
  output [7:0] XOR,
  output Overflow_2,
  output Overflow_3
);

  wire and_2_out, and_3_out, and_4_out, and_5_out, and_6_out, and_7_out, and_8_out, and_9_out, and_10_out,
       and_11_out, and_12_out, and_13_out, and_15_out, and_16_out, and_17_out, and_18_out, and_19_out,
       and_20_out, and_21_out, and_22_out, and_23_out, and_24_out, and_25_out, and_26_out, and_27_out,
       calculadora_4_bits_1_cout, Cout_Multiplicador, Cout_SL, Cout_Somador, Cout_Subtrator,
       full_adder_1_cout, full_adder_1_s1, full_adder_2_cout, full_adder_2_s1, full_adder_3_cout,
       full_adder_3_s1, full_adder_4_cout, full_adder_4_s1, full_adder_5_cout, full_adder_5_s1,
       full_adder_6_cout, full_adder_6_s1, full_adder_7_cout, half_adder_1_carry, half_adder_2_carry,
       half_adder_3_carry, half_adder_4_carry, multiplexer_2_out, or_2_out, or_3_out, or_4_out, xor_2_out,
       xor_4_out, xor_6_out, xor_8_out, xor_10_out, xor_12_out, xor_13_out, xor_14_out, xor_15_out,
       xor_16_out, xor_17_out, xor_18_out, xor_19_out;
  wire [7:0] And_t, calculadora_8_bit_2_s_somador, calculadora_8_bit_3_s_somador, multiplexer_1_out,
       Multiplicador_t, Or_t, SL_t, Somador, SR_t, Subtrator, subtrator_8_bits_2_s_subtrator, Xor_t;

  calculadora_8_bit calculadora_8_bit_1 (
    .Cin(1'b0), .A0(A0_12), .A1(A1_12), .A2(A2_12), .A3(A3_12), .A4(A4_9), .A5(A5_9), .A6(A6_9), .A7(A7_9),
    .B0(B0_10), .B1(B1_10), .B2(B2_10), .B3(B3_10), .B4(B4_7), .B5(B5_7), .B6(B6_7), .B7(B7_7),
    .S_Somador(Somador), .Cout(Cout_Somador));
  xor xor_1 (Soma, A, B);
  and and_1 (Carry, A, B);
  subtrator_8_bits subtrator_8_bits_1 (
    .A0(A0_12), .A1(A1_12), .A2(A2_12), .A3(A3_12), .A4(A4_9), .A5(A5_9), .A6(A6_9), .A7(A7_9), .B0(B0_10),
    .B1(B1_10), .B2(B2_10), .B3(B3_10), .B4(B4_7), .B5(B5_7), .B6(B6_7), .B7(B7_7), .S_Subtrator(Subtrator),
    .Cout(Cout_Subtrator));
  xor xor_2 (xor_2_out, A_2, B_2);
  and and_2 (and_2_out, A_2, B_2);
  xor xor_3 (Soma_2, xor_2_out, Cin);
  and and_3 (and_3_out, xor_2_out, Cin);
  or or_1 (Carry_Out, and_2_out, and_3_out);
  multiplicador multiplicador_1 (
    .A0(A0_12), .A1(A1_12), .A2(A2_12), .A3(A3_12), .B0(B0_10), .B1(B1_10), .B2(B2_10), .B3(B3_10),
    .Multiplicador(Multiplicador_t), .Overflow(Cout_Multiplicador));
  shift_right shift_right_1 (
    .A0(A0_12), .A1(A1_12), .A2(A2_12), .A3(A3_12), .A4(A4_9), .A5(A5_9), .A6(A6_9), .A7(A7_9), .SR(SR_t));
  xor xor_4 (xor_4_out, A0, B0);
  and and_4 (and_4_out, A0, B0);
  xor xor_5 (S0, xor_4_out, 1'b0);
  and and_5 (and_5_out, xor_4_out, 1'b0);
  or or_2 (or_2_out, and_4_out, and_5_out);
  shift_left shift_left_1 (
    .A0(A0_12), .A1(A1_12), .A2(A2_12), .A3(A3_12), .A4(A4_9), .A5(A5_9), .A6(A6_9), .A7(A7_9), .SL(SL_t),
    .Cout(Cout_SL));
  xor xor_6 (xor_6_out, A1, B1);
  and and_6 (and_6_out, A1, B1);
  xor xor_7 (S1, xor_6_out, or_2_out);
  and and_7 (and_7_out, xor_6_out, or_2_out);
  or or_3 (or_3_out, and_6_out, and_7_out);
  operacao_and operacao_and_1 (
    .A0(A0_12), .A1(A1_12), .A2(A2_12), .A3(A3_12), .A4(A4_9), .A5(A5_9), .A6(A6_9), .A7(A7_9), .B0(B0_10),
    .B1(B1_10), .B2(B2_10), .B3(B3_10), .B4(B4_7), .B5(B5_7), .B6(B6_7), .B7(B7_7), .And(And_t));
  xor xor_8 (xor_8_out, A2, B2);
  and and_8 (and_8_out, A2, B2);
  xor xor_9 (S2, xor_8_out, or_3_out);
  and and_9 (and_9_out, xor_8_out, or_3_out);
  or or_4 (or_4_out, and_8_out, and_9_out);
  xor xor_10 (xor_10_out, A3, B3);
  and and_10 (and_10_out, A3, B3);
  operacao_or operacao_or_1 (
    .A0(A0_12), .A1(A1_12), .A2(A2_12), .A3(A3_12), .A4(A4_9), .A5(A5_9), .A6(A6_9), .A7(A7_9), .B0(B0_10),
    .B1(B1_10), .B2(B2_10), .B3(B3_10), .B4(B4_7), .B5(B5_7), .B6(B6_7), .B7(B7_7), .Or(Or_t));
  xor xor_11 (S3, xor_10_out, or_4_out);
  and and_11 (and_11_out, xor_10_out, or_4_out);
  or or_5 (OVERFLOW, and_10_out, and_11_out);
  Seven_Seg_Hex seven_seg_hex_1 (.d({S3, S0, S2, S1}), .dp(1'b0));
  operacao_xor operacao_xor_1 (
    .A0(A0_12), .A1(A1_12), .A2(A2_12), .A3(A3_12), .A4(A4_9), .A5(A5_9), .A6(A6_9), .A7(A7_9), .B0(B0_10),
    .B1(B1_10), .B2(B2_10), .B3(B3_10), .B4(B4_7), .B5(B5_7), .B6(B6_7), .B7(B7_7), .Xor(Xor_t));
  calculadora_4_bits calculadora_4_bits_1 (
    .Cin(Cin_6), .A0(A0_2), .A1(A1_2), .A2(A2_2), .A3(A3_2), .B0(B0_2), .B1(B1_2), .B2(B2_2), .B3(B3_2),
    .S0(S0_2), .S1(S1_2), .S2(S2_2), .S3(S3_2), .Cout(calculadora_4_bits_1_cout));
  calculadora_4_bits calculadora_4_bits_2 (
    .Cin(calculadora_4_bits_1_cout), .A0(A4), .A1(A5), .A2(A6), .A3(A7), .B0(B4), .B1(B5), .B2(B6), .B3(B7),
    .S0(S4), .S1(S5), .S2(S6), .S3(S7), .Cout(Cout));
  Multiplexer #(.Bits(8), .Selector_Bits(3)) multiplexer_1 (
    .sel({SEL_2, SEL_1, SEL_0}), .in_0(Somador), .in_1(Subtrator), .in_2(Multiplicador_t), .in_3(SR_t),
    .in_4(SL_t), .in_5(And_t), .in_6(Or_t), .in_7(Xor_t), .out(multiplexer_1_out));
  Seven_Seg_Hex seven_seg_hex_2 (.d(multiplexer_1_out[7:4]), .dp(1'b0));
  Seven_Seg_Hex seven_seg_hex_3 (.d(multiplexer_1_out[3:0]), .dp(1'b0));
  Multiplexer #(.Selector_Bits(3)) multiplexer_2 (
    .sel({SEL_2, SEL_1, SEL_0}), .in_0(Cout_Somador), .in_1(Cout_Subtrator), .in_2(Cout_Multiplicador),
    .in_3(1'b0), .in_4(Cout_SL), .in_5(1'b0), .in_6(1'b0), .in_7(1'b0), .out(multiplexer_2_out));
  LED led_1 (.in(multiplexer_2_out));
  calculadora_8_bit calculadora_8_bit_2 (
    .Cin(Cin_7), .A0(A8), .A1(A9), .A2(A10), .A3(A11), .A4(A12), .A5(A13), .A6(A14), .A7(A15), .B0(B8),
    .B1(B9), .B2(B10), .B3(B11), .B4(B12), .B5(B13), .B6(B14), .B7(B15),
    .S_Somador(calculadora_8_bit_2_s_somador), .Cout(out_78));
  Seven_Seg_Hex seven_seg_hex_4 (.d(calculadora_8_bit_2_s_somador[7:4]), .dp(1'b0));
  Seven_Seg_Hex seven_seg_hex_5 (.d(calculadora_8_bit_2_s_somador[3:0]), .dp(1'b0));
  xor xor_12 (xor_12_out, B0_3, Sub);
  xor xor_13 (xor_13_out, B1_3, Sub);
  xor xor_14 (xor_14_out, B2_3, Sub);
  xor xor_15 (xor_15_out, B3_3, Sub);
  xor xor_16 (xor_16_out, B4_2, Sub);
  xor xor_17 (xor_17_out, B5_2, Sub);
  xor xor_18 (xor_18_out, B6_2, Sub);
  xor xor_19 (xor_19_out, B7_2, Sub);
  calculadora_8_bit calculadora_8_bit_3 (
    .Cin(Sub), .A0(A0_3), .A1(A1_3), .A2(A2_3), .A3(A3_3), .A4(A4_2), .A5(A5_2), .A6(A6_2), .A7(A7_2),
    .B0(xor_12_out), .B1(xor_13_out), .B2(xor_14_out), .B3(xor_15_out), .B4(xor_16_out), .B5(xor_17_out),
    .B6(xor_18_out), .B7(xor_19_out), .S_Somador(calculadora_8_bit_3_s_somador), .Cout(out_95));
  Seven_Seg_Hex seven_seg_hex_6 (.d(calculadora_8_bit_3_s_somador[7:4]), .dp(1'b0));
  Seven_Seg_Hex seven_seg_hex_7 (.d(calculadora_8_bit_3_s_somador[3:0]), .dp(1'b0));
  subtrator_8_bits subtrator_8_bits_2 (
    .A0(A0_4), .A1(A1_4), .A2(A2_4), .A3(A3_4), .A4(A4_3), .A5(A5_3), .A6(A6_3), .A7(A7_3), .B0(B0_4),
    .B1(B1_4), .B2(B2_4), .B3(B3_4), .B4(B4_3), .B5(B5_3), .B6(B6_3), .B7(B7_3),
    .S_Subtrator(subtrator_8_bits_2_s_subtrator), .Cout(Cout_2));
  Seven_Seg_Hex seven_seg_hex_8 (.d(subtrator_8_bits_2_s_subtrator[7:4]), .dp(1'b0));
  Seven_Seg_Hex seven_seg_hex_9 (.d(subtrator_8_bits_2_s_subtrator[3:0]), .dp(1'b0));
  and and_12 (and_12_out, A0_5, B2_5);
  and and_13 (and_13_out, A0_5, B3_5);
  and and_14 (MULT_BIT0, A0_5, B0_5);
  and and_15 (and_15_out, A0_5, B1_5);
  and and_16 (and_16_out, A1_5, B1_5);
  and and_17 (and_17_out, A1_5, B2_5);
  and and_18 (and_18_out, A1_5, B3_5);
  and and_19 (and_19_out, A1_5, B0_5);
  and and_20 (and_20_out, A2_5, B2_5);
  and and_21 (and_21_out, A2_5, B3_5);
  and and_22 (and_22_out, A2_5, B0_5);
  and and_23 (and_23_out, A2_5, B1_5);
  and and_24 (and_24_out, A3_5, B1_5);
  and and_25 (and_25_out, A3_5, B2_5);
  and and_26 (and_26_out, A3_5, B3_5);
  and and_27 (and_27_out, A3_5, B0_5);
  half_adder half_adder_1 (.A(and_19_out), .B(and_15_out), .Soma(MULT_BIT1), .Carry(half_adder_1_carry));
  full_adder full_adder_1 (
    .Cin(half_adder_1_carry), .A(and_22_out), .B(and_16_out), .S1(full_adder_1_s1), .Cout(full_adder_1_cout));
  half_adder half_adder_2 (.A(full_adder_1_s1), .B(and_12_out), .Soma(MULT_BIT2), .Carry(half_adder_2_carry));
  full_adder full_adder_2 (
    .Cin(full_adder_1_cout), .A(and_27_out), .B(and_23_out), .S1(full_adder_2_s1), .Cout(full_adder_2_cout));
  full_adder full_adder_3 (
    .Cin(half_adder_2_carry), .A(full_adder_2_s1), .B(and_17_out), .S1(full_adder_3_s1),
    .Cout(full_adder_3_cout));
  half_adder half_adder_3 (.A(full_adder_3_s1), .B(and_13_out), .Soma(MULT_BIT3), .Carry(half_adder_3_carry));
  full_adder full_adder_4 (
    .Cin(full_adder_2_cout), .A(and_24_out), .B(and_20_out), .S1(full_adder_4_s1), .Cout(full_adder_4_cout));
  full_adder full_adder_5 (
    .Cin(full_adder_3_cout), .A(full_adder_4_s1), .B(and_18_out), .S1(full_adder_5_s1),
    .Cout(full_adder_5_cout));
  full_adder full_adder_6 (
    .Cin(full_adder_4_cout), .A(and_25_out), .B(and_21_out), .S1(full_adder_6_s1), .Cout(full_adder_6_cout));
  half_adder half_adder_4 (.A(full_adder_5_s1), .B(half_adder_3_carry), .Soma(MULT_BIT4), .Carry(half_adder_4_carry));
  full_adder full_adder_7 (
    .Cin(half_adder_4_carry), .A(full_adder_6_s1), .B(full_adder_5_cout), .S1(MULT_BIT5),
    .Cout(full_adder_7_cout));
  full_adder full_adder_8 (
    .Cin(full_adder_7_cout), .A(and_26_out), .B(full_adder_6_cout), .S1(MULT_BIT6), .Cout(MULT_BIT7));
  multiplicador multiplicador_2 (
    .A0(A0_6), .A1(A1_6), .A2(A2_6), .A3(A3_6), .B0(B0_6), .B1(B1_6), .B2(B2_6), .B3(B3_6),
    .Multiplicador(Multiplicador), .Overflow(Overflow_2));
  shift_right shift_right_2 (.A0(A16), .A1(A17), .A2(A18), .A3(A19), .A4(A20), .A5(A21), .A6(A22), .A7(A23), .SR(SR));
  shift_left shift_left_2 (
    .A0(A24), .A1(A25), .A2(A26), .A3(A27), .A4(A28), .A5(A29), .A6(A30), .A7(A31), .SL(SL), .Cout(Overflow_3));
  xor xor_20 (XOR_BIT0, A0_11, B0_9);
  xor xor_21 (XOR_BIT1, A1_11, B1_9);
  xor xor_22 (XOR_BIT2, A2_11, B2_9);
  xor xor_23 (XOR_BIT3, A3_11, B3_9);
  xor xor_24 (XOR_BIT4, A4_8, B4_6);
  xor xor_25 (XOR_BIT5, A5_8, B5_6);
  xor xor_26 (XOR_BIT6, A6_8, B6_6);
  xor xor_27 (XOR_BIT7, A7_8, B7_6);
  and and_28 (AND_BIT0, A0_9, B0_7);
  and and_29 (AND_BIT1, A1_9, B1_7);
  and and_30 (AND_BIT2, A2_9, B2_7);
  and and_31 (AND_BIT3, A3_9, B3_7);
  and and_32 (AND_BIT4, A4_6, B4_4);
  and and_33 (AND_BIT5, A5_6, B5_4);
  and and_34 (AND_BIT6, A6_6, B6_4);
  and and_35 (AND_BIT7, A7_6, B7_4);
  or or_6 (OR_BIT0, A0_10, B0_8);
  or or_7 (OR_BIT1, A1_10, B1_8);
  or or_8 (OR_BIT2, A2_10, B2_8);
  or or_9 (OR_BIT3, A3_10, B3_8);
  or or_10 (OR_BIT4, A4_7, B4_5);
  or or_11 (OR_BIT5, A5_7, B5_5);
  or or_12 (OR_BIT6, A6_7, B6_5);
  or or_13 (OR_BIT7, A7_7, B7_5);
  operacao_and operacao_and_2 (
    .A0(A32), .A1(A33), .A2(A34), .A3(A35), .A4(A36), .A5(A37), .A6(A38), .A7(A39), .B0(B16), .B1(B17),
    .B2(B18), .B3(B19), .B4(B20), .B5(B21), .B6(B22), .B7(B23), .And(AND));
  operacao_or operacao_or_2 (
    .A0(A40), .A1(A41), .A2(A42), .A3(A43), .A4(A44), .A5(A45), .A6(A46), .A7(A47), .B0(B24), .B1(B25),
    .B2(B26), .B3(B27), .B4(B28), .B5(B29), .B6(B30), .B7(B31), .Or(OR));
  operacao_xor operacao_xor_2 (
    .A0(A48), .A1(A49), .A2(A50), .A3(A51), .A4(A52), .A5(A53), .A6(A54), .A7(A55), .B0(B32), .B1(B33),
    .B2(B34), .B3(B35), .B4(B36), .B5(B37), .B6(B38), .B7(B39), .Xor(XOR));

  assign SL_BIT0 = 1'b0;
  assign SL_BIT1 = A0_8;
  assign SL_BIT2 = A1_8;
  assign SL_BIT3 = A2_8;
  assign SL_BIT4 = A3_8;
  assign SL_BIT5 = A4_5;
  assign SL_BIT6 = A5_5;
  assign SL_BIT7 = A6_5;
  assign SR_BIT0 = A1_7;
  assign SR_BIT1 = A2_7;
  assign SR_BIT2 = A3_7;
  assign SR_BIT3 = A4_4;
  assign SR_BIT4 = A5_4;
  assign SR_BIT5 = A6_4;
  assign SR_BIT6 = A7_4;
  assign SR_BIT7 = 1'b0;

  // Other names for the same wires on the sheet: A0_MULTI = A0_5; A0_t = A0_12; A1_MULTI = A1_5; A1_t = A1_12;
  //   A2_MULTI = A2_5; A2_t = A2_12; A3_MULTI = A3_5; A3_t = A3_12; A4_t = A4_9; A5_t = A5_9; A6_t = A6_9;
  //   A7_t = A7_9; B0_MULTI = B0_5; B0_t = B0_10; B1_MULTI = B1_5; B1_t = B1_10; B2_MULTI = B2_5; B2_t = B2_10;
  //   B3_MULTI = B3_5; B3_t = B3_10; B4_t = B4_7; B5_t = B5_7; B6_t = B6_7; B7_t = B7_7;
  //   Seleção[2:0] = {SEL_2, SEL_1, SEL_0}

  // Notes on the sheet:
  //   somador de 8 bits
  //   Somador de 1/2 bit
  //   Meio Somador (Half Adder)
  //   Subtrator de 8 bits
  //   Somador Completo (Full Adder)
  //   Somador de 1 bit
  //   MULTIPLICADOR DE 8 BITS
  //   SHIFT RIGHT
  //   Full Adder 0
  //   SHIFT LEFT
  //   Full Adder 1
  //   Somador de 4 bits
  //   OPERAÇÃO AND
  //   Full Adder 2
  //   Full Adder 3
  //   OPERAÇÃO OR
  //   OPERAÇÃO XOR
  //   ALU
  //   2 somadores de 4 bits
  //   ATIVAÇÃO DO ALU
  //   000: Somador
  //   001: Subtrator
  //   010: Multiplicador
  //   011: SR
  //   100: SL
  //   101: And
  //   110: Or
  //   111: Xor
  //   A0·B1
  //   A0·B2
  //   A0·B3
  //   A0·B0
  //   A1·B2
  //   A1·B3
  //   A1·B1
  //   A1·B0
  //   A2·B1
  //   A2·B2
  //   A2·B3
  //   A2·B0
  //   A3·B2
  //   A3·B3
  //   A3·B0
  //   A3·B1
  //   ESQUERDA = MULTIPLICAR POR 2
  //   DIREITA = DIVIDIR POR 2
endmodule
