// Digital circuit calculadora 8 bit.dig as structural Verilog
module calculadora_8_bit (
  input  Cin,
  input  A0,
  input  A1,
  input  A2,
  input  A3,
  input  A4,
  input  A5,
  input  A6,
  input  A7,
  input  B0,
  input  B1,
  input  B2,
  input  B3,
  input  B4,
  input  B5,
  input  B6,
  input  B7,
  output [7:0] S_Somador,
  output Cout
);

  wire calculadora_4_bits_1_cout;

  calculadora_4_bits calculadora_4_bits_1 (
    .Cin(Cin), .A0(A0), .A1(A1), .A2(A2), .A3(A3), .B0(B0), .B1(B1), .B2(B2), .B3(B3), .S0(S_Somador[0]),
    .S1(S_Somador[1]), .S2(S_Somador[2]), .S3(S_Somador[3]), .Cout(calculadora_4_bits_1_cout));
  calculadora_4_bits calculadora_4_bits_2 (
    .Cin(calculadora_4_bits_1_cout), .A0(A4), .A1(A5), .A2(A6), .A3(A7), .B0(B4), .B1(B5), .B2(B6), .B3(B7),
    .S0(S_Somador[4]), .S1(S_Somador[5]), .S2(S_Somador[6]), .S3(S_Somador[7]), .Cout(Cout));
endmodule
