// Digital circuit meio somador.dig as structural Verilog
module meio_somador (
  input  A,
  input  B,
  output Soma,
  output Carry
);

  xor xor_1 (Soma, A, B);
  and and_1 (Carry, A, B);
endmodule
