// Digital circuit multiplicador.dig as structural Verilog
module multiplicador (
  input  A0,
  input  A1,
  input  A2,
  input  A3,
  input  B0,
  input  B1,
  input  B2,
  input  B3,
  output [7:0] Multiplicador,
  output Overflow
);

  wire and_1_out, and_2_out, and_4_out, and_5_out, and_6_out, and_7_out, and_8_out, and_9_out, and_10_out,
       and_11_out, and_12_out, and_13_out, and_14_out, and_15_out, and_16_out, full_adder_1_cout,
       full_adder_1_s1, full_adder_2_cout, full_adder_2_s1, full_adder_3_cout, full_adder_3_s1,
       full_adder_4_cout, full_adder_4_s1, full_adder_5_cout, full_adder_5_s1, full_adder_6_cout,
       full_adder_6_s1, full_adder_7_cout, half_adder_1_carry, half_adder_2_carry, half_adder_3_carry,
       half_adder_4_carry;

  and and_1 (and_1_out, A0, B2);
  and and_2 (and_2_out, A0, B3);
  and and_3 (Multiplicador[0], A0, B0);
  and and_4 (and_4_out, A0, B1);
  and and_5 (and_5_out, A1, B1);
  and and_6 (and_6_out, A1, B2);
  and and_7 (and_7_out, A1, B3);
  and and_8 (and_8_out, A1, B0);
  and and_9 (and_9_out, A2, B2);
  and and_10 (and_10_out, A2, B3);
  and and_11 (and_11_out, A2, B0);
  and and_12 (and_12_out, A2, B1);
  and and_13 (and_13_out, A3, B1);
  and and_14 (and_14_out, A3, B2);
  and and_15 (and_15_out, A3, B3);
  and and_16 (and_16_out, A3, B0);
  half_adder half_adder_1 (.A(and_8_out), .B(and_4_out), .Soma(Multiplicador[1]), .Carry(half_adder_1_carry));
  full_adder full_adder_1 (
    .Cin(half_adder_1_carry), .A(and_11_out), .B(and_5_out), .S1(full_adder_1_s1), .Cout(full_adder_1_cout));
  half_adder half_adder_2 (.A(full_adder_1_s1), .B(and_1_out), .Soma(Multiplicador[2]), .Carry(half_adder_2_carry));
  full_adder full_adder_2 (
    .Cin(full_adder_1_cout), .A(and_16_out), .B(and_12_out), .S1(full_adder_2_s1), .Cout(full_adder_2_cout));
  full_adder full_adder_3 (
    .Cin(half_adder_2_carry), .A(full_adder_2_s1), .B(and_6_out), .S1(full_adder_3_s1),
    .Cout(full_adder_3_cout));
  half_adder half_adder_3 (.A(full_adder_3_s1), .B(and_2_out), .Soma(Multiplicador[3]), .Carry(half_adder_3_carry));
  full_adder full_adder_4 (
    .Cin(full_adder_2_cout), .A(and_13_out), .B(and_9_out), .S1(full_adder_4_s1), .Cout(full_adder_4_cout));
  full_adder full_adder_5 (
    .Cin(full_adder_3_cout), .A(full_adder_4_s1), .B(and_7_out), .S1(full_adder_5_s1),
    .Cout(full_adder_5_cout));
  full_adder full_adder_6 (
    .Cin(full_adder_4_cout), .A(and_14_out), .B(and_10_out), .S1(full_adder_6_s1), .Cout(full_adder_6_cout));
  half_adder half_adder_4 (
    .A(full_adder_5_s1), .B(half_adder_3_carry), .Soma(Multiplicador[4]), .Carry(half_adder_4_carry));
  full_adder full_adder_7 (
    .Cin(half_adder_4_carry), .A(full_adder_6_s1), .B(full_adder_5_cout), .S1(Multiplicador[5]),
    .Cout(full_adder_7_cout));
  full_adder full_adder_8 (
    .Cin(full_adder_7_cout), .A(and_15_out), .B(full_adder_6_cout), .S1(Multiplicador[6]),
    .Cout(Multiplicador[7]));
  or or_1 (Overflow, Multiplicador[4], Multiplicador[5], Multiplicador[6], Multiplicador[7]);

  // Notes on the sheet:
  //   A0·B1
  //   A0·B2
  //   A0·B3
  //   A0·B0
  //   A1·B2
  //   A1·B3
  //   A1·B1
  //   A1·B0
  //   A2·B1
  //   A2·B2
  //   A2·B3
  //   A2·B0
  //   A3·B2
  //   A3·B3
  //   A3·B0
  //   A3·B1
  //   MULTIPLICADOR DE 8 BITS
endmodule
