// Digital circuit operacao and.dig as structural Verilog
module operacao_and (
  input  A0,
  input  A1,
  input  A2,
  input  A3,
  input  A4,
  input  A5,
  input  A6,
  input  A7,
  input  B0,
  input  B1,
  input  B2,
  input  B3,
  input  B4,
  input  B5,
  input  B6,
  input  B7,
  output [7:0] And
);

  and and_1 (And[0], A0, B0);
  and and_2 (And[1], A1, B1);
  and and_3 (And[2], A2, B2);
  and and_4 (And[3], A3, B3);
  and and_5 (And[4], A4, B4);
  and and_6 (And[5], A5, B5);
  and and_7 (And[6], A6, B6);
  and and_8 (And[7], A7, B7);

  // Notes on the sheet:
  //   OPERAÇÃO AND
endmodule
