// Digital circuit operacao or.dig as structural Verilog
module operacao_or (
  input  A0,
  input  A1,
  input  A2,
  input  A3,
  input  A4,
  input  A5,
  input  A6,
  input  A7,
  input  B0,
  input  B1,
  input  B2,
  input  B3,
  input  B4,
  input  B5,
  input  B6,
  input  B7,
  output [7:0] Or
);

  or or_1 (Or[0], A0, B0);
  or or_2 (Or[1], A1, B1);
  or or_3 (Or[2], A2, B2);
  or or_4 (Or[3], A3, B3);
  or or_5 (Or[4], A4, B4);
  or or_6 (Or[5], A5, B5);
  or or_7 (Or[6], A6, B6);
  or or_8 (Or[7], A7, B7);

  // Notes on the sheet:
  //   OPERAÇÃO OR
endmodule
