// Digital circuit operacao xor.dig as structural Verilog
module operacao_xor (
  input  A0,
  input  A1,
  input  A2,
  input  A3,
  input  A4,
  input  A5,
  input  A6,
  input  A7,
  input  B0,
  input  B1,
  input  B2,
  input  B3,
  input  B4,
  input  B5,
  input  B6,
  input  B7,
  output [7:0] Xor
);

  xor xor_1 (Xor[0], A0, B0);
  xor xor_2 (Xor[1], A1, B1);
  xor xor_3 (Xor[2], A2, B2);
  xor xor_4 (Xor[3], A3, B3);
  xor xor_5 (Xor[4], A4, B4);
  xor xor_6 (Xor[5], A5, B5);
  xor xor_7 (Xor[6], A6, B6);
  xor xor_8 (Xor[7], A7, B7);

  // Notes on the sheet:
  //   OPERAÇÃO XOR
endmodule
