// Digital circuit shift left.dig as structural Verilog
module shift_left (
  input  A0,
  input  A1,
  input  A2,
  input  A3,
  input  A4,
  input  A5,
  input  A6,
  input  A7,
  output [7:0] SL,
  output Cout
);


  assign Cout = 1'b0;
  assign SL = {A6, A5, A4, A3, A2, A1, A0, 1'b0};

  // Notes on the sheet:
  //   SHIFT LEFT
endmodule
