// Digital circuit shift right.dig as structural Verilog
module shift_right (
  input  A0,
  input  A1,
  input  A2,
  input  A3,
  input  A4,
  input  A5,
  input  A6,
  input  A7,
  output [7:0] SR
);


  assign SR = {1'b0, A7, A6, A5, A4, A3, A2, A1};
endmodule
