// Digital circuit subtrator 8 bits.dig as structural Verilog
module subtrator_8_bits (
  input  A0,
  input  A1,
  input  A2,
  input  A3,
  input  A4,
  input  A5,
  input  A6,
  input  A7,
  input  B0,
  input  B1,
  input  B2,
  input  B3,
  input  B4,
  input  B5,
  input  B6,
  input  B7,
  output [7:0] S_Subtrator,
  output Cout
);

  wire xor_1_out, xor_2_out, xor_3_out, xor_4_out, xor_5_out, xor_6_out, xor_7_out, xor_8_out;

  xor xor_1 (xor_1_out, B0, 1'b1);
  xor xor_2 (xor_2_out, B1, 1'b1);
  xor xor_3 (xor_3_out, B2, 1'b1);
  xor xor_4 (xor_4_out, B3, 1'b1);
  xor xor_5 (xor_5_out, B4, 1'b1);
  xor xor_6 (xor_6_out, B5, 1'b1);
  xor xor_7 (xor_7_out, B6, 1'b1);
  xor xor_8 (xor_8_out, B7, 1'b1);
  calculadora_8_bit calculadora_8_bit_1 (
    .Cin(1'b1), .A0(A0), .A1(A1), .A2(A2), .A3(A3), .A4(A4), .A5(A5), .A6(A6), .A7(A7), .B0(xor_1_out),
    .B1(xor_2_out), .B2(xor_3_out), .B3(xor_4_out), .B4(xor_5_out), .B5(xor_6_out), .B6(xor_7_out),
    .B7(xor_8_out), .S_Somador(S_Subtrator), .Cout(Cout));
endmodule
